// Logisim project Parinda Rahman_1931804042.circ as structural Verilog
module _0_59_Counter (
  input  in_1,
  output q0,
  output q1,
  output [5:0] out_4,
  output out_5,
  output out_6,
  output q4,
  output q5,
  output out_9
);

  wire d_ff_1_qn, d_ff_2_qn, d_ff_3_qn, d_ff_4_qn, d_ff_5_qn, d_ff_6_qn;

  D_Flip_Flop d_ff_1 (.clk(in_1), .D(d_ff_1_qn), .Q(out_4[0]), .Qn(d_ff_1_qn), .reset(out_9));  // open: preset, en
  D_Flip_Flop d_ff_2 (.clk(d_ff_1_qn), .D(d_ff_2_qn), .Q(out_4[1]), .Qn(d_ff_2_qn), .reset(out_9));  // open: preset, en
  D_Flip_Flop d_ff_3 (.clk(d_ff_2_qn), .D(d_ff_3_qn), .Q(out_4[2]), .Qn(d_ff_3_qn), .reset(out_9));  // open: preset, en
  D_Flip_Flop d_ff_4 (.clk(d_ff_3_qn), .D(d_ff_4_qn), .Q(out_4[3]), .Qn(d_ff_4_qn), .reset(out_9));  // open: preset, en
  D_Flip_Flop d_ff_5 (.clk(d_ff_4_qn), .D(d_ff_5_qn), .Q(out_4[4]), .Qn(d_ff_5_qn), .reset(out_9));  // open: preset, en
  D_Flip_Flop d_ff_6 (.clk(d_ff_5_qn), .D(d_ff_6_qn), .Q(out_4[5]), .Qn(d_ff_6_qn), .reset(out_9));  // open: preset, en
  and and_1 (out_9, out_4[5], out_4[4], out_4[3], out_4[2]);

  assign out_5 = out_4[2];
  assign out_6 = out_4[3];
  assign q0 = out_4[0];
  assign q1 = out_4[1];
  assign q4 = out_4[4];
  assign q5 = out_4[5];

  // Notes on the sheet:
  //   q2
  //   q3
endmodule

module BCD_converter (
  input  i0,
  input  i1,
  input  i2,
  input  i3,
  input  i4,
  input  i5,
  output w0,
  output w1,
  output w2,
  output w3,
  output w4,
  output w5,
  output w6,
  output w7
);

  wire and_1_out, and_2_out, and_3_out, and_4_out, and_5_out, and_6_out, and_7_out, and_8_out, and_9_out,
       and_10_out, and_11_out, and_12_out, and_13_out, and_14_out, and_15_out, and_16_out, and_17_out,
       and_18_out, and_19_out, and_20_out, and_21_out, and_22_out, and_23_out, and_24_out, and_25_out,
       and_26_out, and_27_out, and_28_out, and_29_out, and_30_out, and_31_out, and_32_out, and_33_out,
       and_34_out, and_35_out, and_36_out, and_37_out, and_38_out, not_1_out, not_2_out, not_3_out,
       not_4_out, not_5_out, not_6_out, not_7_out, not_8_out, not_9_out, not_10_out, not_11_out, not_12_out,
       not_13_out, not_14_out, not_15_out, not_16_out, not_17_out, not_18_out, not_19_out, not_20_out,
       not_21_out, not_22_out, not_23_out, not_24_out, not_25_out, not_26_out, not_27_out, not_28_out,
       not_29_out, not_30_out, not_31_out, not_32_out, not_33_out, not_34_out, not_35_out, not_36_out,
       not_37_out, not_38_out, not_39_out, not_40_out, not_41_out, not_42_out, not_43_out, not_44_out,
       not_45_out, not_46_out, not_47_out, not_48_out, not_49_out, not_50_out, not_51_out, not_52_out,
       not_53_out, not_54_out, not_55_out, not_56_out, not_57_out, not_58_out, not_59_out, not_60_out,
       not_61_out, not_62_out, not_63_out, not_64_out, not_65_out, not_66_out, not_67_out, not_68_out,
       not_69_out, not_70_out, not_71_out;

  and and_1 (and_1_out, i0, i2);
  and and_2 (and_2_out, i0, i1);
  not not_1 (not_1_out, i0);
  not not_2 (not_2_out, i0);
  not not_3 (not_3_out, i1);
  not not_4 (not_4_out, i2);
  not not_5 (not_5_out, i0);
  not not_6 (not_6_out, i1);
  not not_7 (not_7_out, i0);
  not not_8 (not_8_out, i1);
  not not_9 (not_9_out, i0);
  not not_10 (not_10_out, i0);
  not not_11 (not_11_out, i2);
  not not_12 (not_12_out, i3);
  not not_13 (not_13_out, i1);
  not not_14 (not_14_out, i2);
  not not_15 (not_15_out, i2);
  not not_16 (not_16_out, i2);
  not not_17 (not_17_out, i3);
  not not_18 (not_18_out, i0);
  not not_19 (not_19_out, i1);
  not not_20 (not_20_out, i3);
  not not_21 (not_21_out, i4);
  not not_22 (not_22_out, i0);
  not not_23 (not_23_out, i2);
  not not_24 (not_24_out, i3);
  not not_25 (not_25_out, i0);
  not not_26 (not_26_out, i4);
  not not_27 (not_27_out, i1);
  not not_28 (not_28_out, i2);
  not not_29 (not_29_out, i2);
  not not_30 (not_30_out, i3);
  not not_31 (not_31_out, i4);
  not not_32 (not_32_out, i3);
  not not_33 (not_33_out, i1);
  not not_34 (not_34_out, i2);
  not not_35 (not_35_out, i4);
  not not_36 (not_36_out, i0);
  not not_37 (not_37_out, i1);
  not not_38 (not_38_out, i0);
  not not_39 (not_39_out, i3);
  not not_40 (not_40_out, i4);
  not not_41 (not_41_out, i0);
  not not_42 (not_42_out, i3);
  not not_43 (not_43_out, i3);
  not not_44 (not_44_out, i4);
  not not_45 (not_45_out, i1);
  not not_46 (not_46_out, i2);
  not not_47 (not_47_out, i3);
  not not_48 (not_48_out, i1);
  not not_49 (not_49_out, i2);
  not not_50 (not_50_out, i0);
  not not_51 (not_51_out, i1);
  not not_52 (not_52_out, i2);
  not not_53 (not_53_out, i0);
  not not_54 (not_54_out, i2);
  not not_55 (not_55_out, i0);
  not not_56 (not_56_out, i1);
  not not_57 (not_57_out, i4);
  not not_58 (not_58_out, i0);
  not not_59 (not_59_out, i2);
  not not_60 (not_60_out, i3);
  not not_61 (not_61_out, i4);
  not not_62 (not_62_out, i0);
  not not_63 (not_63_out, i3);
  not not_64 (not_64_out, i1);
  not not_65 (not_65_out, i2);
  not not_66 (not_66_out, i4);
  not not_67 (not_67_out, i2);
  not not_68 (not_68_out, i4);
  not not_69 (not_69_out, i1);
  not not_70 (not_70_out, i3);
  not not_71 (not_71_out, i4);
  or or_1 (w1, and_1_out, and_2_out);
  and and_3 (and_3_out, not_1_out, i1, i3);
  and and_4 (and_4_out, not_2_out, i1, i2);
  and and_5 (and_5_out, i1, i2, i3);
  and and_6 (and_6_out, i0, not_3_out, not_4_out);
  and and_7 (and_7_out, not_5_out, not_6_out, i2, i4);
  and and_8 (and_8_out, not_7_out, not_8_out, i2, i3);
  and and_9 (and_9_out, not_9_out, i2, i3, i4);
  and and_10 (and_10_out, not_10_out, i1, not_11_out, not_12_out);
  and and_11 (and_11_out, i0, not_13_out, not_14_out);
  and and_12 (and_12_out, i0, not_15_out, i4);
  and and_13 (and_13_out, i0, not_16_out, i3);
  and and_14 (and_14_out, i0, i1, i2, not_17_out);
  and and_15 (and_15_out, not_18_out, not_19_out, i2, not_20_out, not_21_out);
  and and_16 (and_16_out, not_22_out, i1, not_23_out, not_24_out, i4);
  and and_17 (and_17_out, not_25_out, i1, i2, i3, not_26_out);
  and and_18 (and_18_out, i0, not_27_out, not_28_out, i3, i4);
  and and_19 (and_19_out, i0, i1, not_29_out, not_30_out, not_31_out);
  and and_20 (and_20_out, i0, i1, i2, not_32_out, i4);
  and and_21 (and_21_out, not_33_out, not_34_out, i3, not_35_out);
  and and_22 (and_22_out, not_36_out, not_37_out, i3, i4);
  and and_23 (and_23_out, not_38_out, i1, not_39_out, not_40_out);
  and and_24 (and_24_out, not_41_out, i1, i2, not_42_out);
  and and_25 (and_25_out, i1, i2, not_43_out, not_44_out);
  and and_26 (and_26_out, i0, not_45_out, not_46_out, not_47_out, i4);
  and and_27 (and_27_out, i0, not_48_out, i2, i3);
  and and_28 (and_28_out, i0, i1, not_49_out, i3, i4);
  and and_29 (and_29_out, not_50_out, not_51_out, not_52_out, i4);
  and and_30 (and_30_out, not_53_out, not_54_out, i3, i4);
  and and_31 (and_31_out, not_55_out, not_56_out, i2, i3, not_57_out);
  and and_32 (and_32_out, not_58_out, i1, not_59_out, not_60_out, not_61_out);
  and and_33 (and_33_out, not_62_out, i1, i2, not_63_out, i4);
  and and_34 (and_34_out, i0, not_64_out, not_65_out, not_66_out);
  and and_35 (and_35_out, i0, not_67_out, i3, not_68_out);
  and and_36 (and_36_out, i0, not_69_out, i2, i4);
  and and_37 (and_37_out, i0, i2, i3, i4);
  and and_38 (and_38_out, i0, i1, i2, not_70_out, not_71_out);
  or or_2 (w2, and_3_out, and_4_out, and_5_out, and_6_out);
  or or_3 (w3, and_7_out, and_8_out, and_9_out, and_10_out, and_11_out, and_12_out, and_13_out, and_14_out);
  or or_4 (w4, and_15_out, and_16_out, and_17_out, and_18_out, and_19_out, and_20_out);
  or or_5 (w5, and_21_out, and_22_out, and_23_out, and_24_out, and_25_out, and_26_out, and_27_out, and_28_out);
  or or_6 (w6, and_29_out, and_30_out, and_31_out, and_32_out, and_33_out, and_34_out, and_35_out, and_36_out, and_37_out, and_38_out);

  assign w0 = 1'b0;
  assign w7 = i5;
endmodule

module Decimal_to_7segment (
  input  D,
  input  C,
  input  B,
  input  A,
  output a_2,
  output b_2,
  output c_2,
  output d_2,
  output e,
  output f,
  output g
);

  wire and_1_out, and_2_out, and_3_out, and_4_out, and_5_out, and_6_out, and_7_out, and_8_out, and_9_out,
       and_10_out, and_11_out, and_12_out, and_13_out, and_14_out, and_15_out, and_16_out, not_1_out,
       not_2_out, not_3_out, not_4_out, not_5_out, not_6_out, not_7_out, not_8_out, not_9_out, not_10_out,
       not_11_out, not_12_out, not_13_out, not_14_out, not_15_out, not_16_out, not_17_out, not_18_out,
       not_19_out, not_20_out, not_21_out, undriven;

  not not_1 (not_1_out, C);
  and and_1 (and_1_out, not_1_out, not_2_out);
  not not_2 (not_2_out, A);
  and and_2 (and_2_out, C, A);
  not not_3 (not_3_out, C);
  not not_4 (not_4_out, B);
  and and_3 (and_3_out, not_4_out, not_5_out);
  not not_5 (not_5_out, A);
  and and_4 (and_4_out, B, A);
  not not_6 (not_6_out, B);
  or or_1 (c_2, not_6_out, A, C);
  not not_7 (not_7_out, C);
  and and_5 (and_5_out, not_7_out, not_8_out);
  not not_8 (not_8_out, A);
  not not_9 (not_9_out, C);
  and and_6 (and_6_out, not_9_out, B);
  and and_7 (and_7_out, B, not_10_out);
  not not_10 (not_10_out, A);
  not not_11 (not_11_out, B);
  and and_8 (and_8_out, C, not_11_out, A);
  not not_12 (not_12_out, C);
  and and_9 (and_9_out, not_12_out, not_13_out);
  not not_13 (not_13_out, A);
  and and_10 (and_10_out, B, not_14_out);
  not not_14 (not_14_out, A);
  not not_15 (not_15_out, B);
  and and_11 (and_11_out, not_15_out, not_16_out);
  not not_16 (not_16_out, A);
  and and_12 (and_12_out, C, not_17_out);
  not not_17 (not_17_out, B);
  and and_13 (and_13_out, C, not_18_out);
  not not_18 (not_18_out, A);
  not not_19 (not_19_out, C);
  and and_14 (and_14_out, not_19_out, B);
  and and_15 (and_15_out, C, not_20_out);
  not not_20 (not_20_out, B);
  and and_16 (and_16_out, C, not_21_out);
  not not_21 (not_21_out, A);
  or or_2 (a_2, and_1_out, B, and_2_out, D);
  or or_3 (b_2, not_3_out, and_3_out, and_4_out);
  or or_4 (d_2, and_5_out, and_6_out, and_7_out, and_8_out, D);
  or or_5 (e, and_9_out, and_10_out);
  or or_6 (f, and_11_out, and_12_out, and_13_out, D);
  or or_7 (g, and_14_out, and_15_out, and_16_out, D);
  _7_Segment_Display u_7_segment_display_1 (.g(g), .f(f), .a(a_2), .b(b_2), .e(e), .d(d_2), .c(c_2), .dp(undriven));
endmodule

module _7_segment_with_decoder (
  input  [3:0] in_1
);

  wire decoder_1_out0, decoder_1_out1, decoder_1_out2, decoder_1_out3, decoder_1_out4, decoder_1_out5,
       decoder_1_out6, decoder_1_out7, decoder_1_out8, decoder_1_out9;

  _7_Segment_Display u_7_segment_display_1 (
    .g(decoder_1_out9), .f(decoder_1_out9), .a(decoder_1_out9), .b(decoder_1_out9), .d(decoder_1_out9),
    .c(decoder_1_out9));  // open: e, dp
  _7_Segment_Display u_7_segment_display_2 (
    .g(decoder_1_out8), .f(decoder_1_out8), .a(decoder_1_out8), .b(decoder_1_out8), .e(decoder_1_out8),
    .d(decoder_1_out8), .c(decoder_1_out8));  // open: dp
  _7_Segment_Display u_7_segment_display_3 (
    .a(decoder_1_out7), .b(decoder_1_out7), .c(decoder_1_out7));  // open: g, f, e, d, dp
  Decoder #(.select(4)) decoder_1 (
    .out0(decoder_1_out0), .out1(decoder_1_out1), .out2(decoder_1_out2), .out3(decoder_1_out3),
    .out4(decoder_1_out4), .out5(decoder_1_out5), .out6(decoder_1_out6), .out7(decoder_1_out7),
    .out8(decoder_1_out8), .out9(decoder_1_out9), .sel(in_1));  // open: out10, out11, out12, out13, out14, out15, en
  _7_Segment_Display u_7_segment_display_4 (
    .g(decoder_1_out6), .f(decoder_1_out6), .a(decoder_1_out6), .e(decoder_1_out6), .d(decoder_1_out6),
    .c(decoder_1_out6));  // open: b, dp
  _7_Segment_Display u_7_segment_display_5 (
    .g(decoder_1_out5), .f(decoder_1_out5), .a(decoder_1_out5), .d(decoder_1_out5), .c(decoder_1_out5));  // open: b, e, dp
  _7_Segment_Display u_7_segment_display_6 (
    .g(decoder_1_out4), .f(decoder_1_out4), .b(decoder_1_out4), .c(decoder_1_out4));  // open: a, e, d, dp
  _7_Segment_Display u_7_segment_display_7 (
    .f(decoder_1_out0), .a(decoder_1_out0), .b(decoder_1_out0), .e(decoder_1_out0), .d(decoder_1_out0),
    .c(decoder_1_out0));  // open: g, dp
  _7_Segment_Display u_7_segment_display_8 (.b(decoder_1_out1), .c(decoder_1_out1));  // open: g, f, a, e, d, dp
  _7_Segment_Display u_7_segment_display_9 (
    .g(decoder_1_out2), .a(decoder_1_out2), .b(decoder_1_out2), .e(decoder_1_out2), .d(decoder_1_out2));  // open: f, c, dp
  _7_Segment_Display u_7_segment_display_10 (
    .g(decoder_1_out3), .a(decoder_1_out3), .b(decoder_1_out3), .d(decoder_1_out3), .c(decoder_1_out3));  // open: f, e, dp
endmodule

module Seconds_Circuit (
  output [5:0] out_1,
  output out_2
);

  wire a0, a1, b0, b1, bcd_converter_1_w0, bcd_converter_1_w1, bcd_converter_1_w2, bcd_converter_1_w3,
       bcd_converter_1_w4, bcd_converter_1_w5, bcd_converter_1_w6, bcd_converter_1_w7, c0, c1, clock_1_out,
       d0, d1, e0, e1, f0, f1, g0, g1;

  Clock clock_1 (.out(clock_1_out));
  _0_59_Counter u_0_59_counter_1 (
    .q0(out_1[0]), .q1(out_1[1]), .out_5(out_1[2]), .out_6(out_1[3]), .q4(out_1[4]), .q5(out_1[5]),
    .in_1(clock_1_out));  // open: out_4, out_9
  BCD_converter bcd_converter_1 (
    .i0(out_1[5]), .i1(out_1[4]), .i2(out_1[3]), .i3(out_1[2]), .i4(out_1[1]), .i5(out_1[0]),
    .w0(bcd_converter_1_w0), .w1(bcd_converter_1_w1), .w2(bcd_converter_1_w2), .w3(bcd_converter_1_w3),
    .w4(bcd_converter_1_w4), .w5(bcd_converter_1_w5), .w6(bcd_converter_1_w6), .w7(bcd_converter_1_w7));
  // combinational_for_60sec combinational_for_60sec_1: pin names not known; wires that end beside it: out_1[5], out_1[4], out_1[3], out_1[2], out_1[1], out_1[0], out_2
  Decimal_to_7segment decimal_to_7segment_1 (
    .D(bcd_converter_1_w4), .C(bcd_converter_1_w5), .B(bcd_converter_1_w6), .A(bcd_converter_1_w7), .a_2(a1),
    .b_2(b1), .c_2(c1), .d_2(d1), .e(e1), .f(f1), .g(g1));
  Decimal_to_7segment decimal_to_7segment_2 (
    .D(bcd_converter_1_w0), .C(bcd_converter_1_w1), .B(bcd_converter_1_w2), .A(bcd_converter_1_w3), .a_2(a0),
    .b_2(b0), .c_2(c0), .d_2(d0), .e(e0), .f(f0), .g(g0));
  _7_Segment_Display u_7_segment_display_1 (.g(g0), .f(f0), .a(a0), .b(b0), .e(e0), .d(d0), .c(c0));  // open: dp
  _7_Segment_Display u_7_segment_display_2 (.g(g1), .f(f1), .a(a1), .b(b1), .e(e1), .d(d1), .c(c1));  // open: dp
endmodule

module _0_24_counter (
  input  in_1,
  output q0,
  output q1,
  output out_4,
  output out_5,
  output q4,
  output [4:0] out_7
);

  wire and_1_out, d_ff_1_qn, d_ff_2_qn, d_ff_3_qn, d_ff_4_qn, d_ff_5_qn;

  D_Flip_Flop d_ff_1 (.clk(in_1), .D(d_ff_1_qn), .Q(out_7[0]), .Qn(d_ff_1_qn), .reset(and_1_out));  // open: preset, en
  D_Flip_Flop d_ff_2 (
    .clk(d_ff_1_qn), .D(d_ff_2_qn), .Q(out_7[1]), .Qn(d_ff_2_qn), .reset(and_1_out));  // open: preset, en
  D_Flip_Flop d_ff_3 (
    .clk(d_ff_2_qn), .D(d_ff_3_qn), .Q(out_4), .Qn(d_ff_3_qn), .reset(and_1_out));  // open: preset, en
  D_Flip_Flop d_ff_4 (
    .clk(d_ff_3_qn), .D(d_ff_4_qn), .Q(out_5), .Qn(d_ff_4_qn), .reset(and_1_out));  // open: preset, en
  D_Flip_Flop d_ff_5 (
    .clk(d_ff_4_qn), .D(d_ff_5_qn), .Q(out_7[4]), .Qn(d_ff_5_qn), .reset(and_1_out));  // open: preset, en
  and and_1 (and_1_out, out_7[4], out_5);

  assign out_7[3:2] = {out_5, out_4};
  assign q0 = out_7[0];
  assign q1 = out_7[1];
  assign q4 = out_7[4];

  // Notes on the sheet:
  //   q2
  //   q3
endmodule

module Minutes_circuit (
);

  wire aa0, aa1, bb0, bb1, bcd_converter_1_w0, bcd_converter_1_w1, bcd_converter_1_w2, bcd_converter_1_w3,
       bcd_converter_1_w4, bcd_converter_1_w5, bcd_converter_1_w6, bcd_converter_1_w7, cc0, cc1, clock_1_out,
       dd0, dd1, ee0, ee1, ff0, ff1, gg0, gg1, n0_59_counter_1_out_5, n0_59_counter_1_out_6,
       n0_59_counter_1_q0, n0_59_counter_1_q1, n0_59_counter_1_q4, n0_59_counter_1_q5;

  Clock clock_1 (.out(clock_1_out));
  _0_59_Counter u_0_59_counter_1 (
    .q0(n0_59_counter_1_q0), .q1(n0_59_counter_1_q1), .out_5(n0_59_counter_1_out_5),
    .out_6(n0_59_counter_1_out_6), .q4(n0_59_counter_1_q4), .q5(n0_59_counter_1_q5), .in_1(clock_1_out));  // open: out_4, out_9
  BCD_converter bcd_converter_1 (
    .i0(n0_59_counter_1_q5), .i1(n0_59_counter_1_q4), .i2(n0_59_counter_1_out_6), .i3(n0_59_counter_1_out_5),
    .i4(n0_59_counter_1_q1), .i5(n0_59_counter_1_q0), .w0(bcd_converter_1_w0), .w1(bcd_converter_1_w1),
    .w2(bcd_converter_1_w2), .w3(bcd_converter_1_w3), .w4(bcd_converter_1_w4), .w5(bcd_converter_1_w5),
    .w6(bcd_converter_1_w6), .w7(bcd_converter_1_w7));
  Decimal_to_7segment decimal_to_7segment_1 (
    .D(bcd_converter_1_w4), .C(bcd_converter_1_w5), .B(bcd_converter_1_w6), .A(bcd_converter_1_w7),
    .a_2(aa1), .b_2(bb1), .c_2(cc1), .d_2(dd1), .e(ee1), .f(ff1), .g(gg1));
  Decimal_to_7segment decimal_to_7segment_2 (
    .D(bcd_converter_1_w0), .C(bcd_converter_1_w1), .B(bcd_converter_1_w2), .A(bcd_converter_1_w3),
    .a_2(aa0), .b_2(bb0), .c_2(cc0), .d_2(dd0), .e(ee0), .f(ff0), .g(gg0));
  _7_Segment_Display u_7_segment_display_1 (.g(gg0), .f(ff0), .a(aa0), .b(bb0), .e(ee0), .d(dd0), .c(cc0));  // open: dp
  _7_Segment_Display u_7_segment_display_2 (.g(gg1), .f(ff1), .a(aa1), .b(bb1), .e(ee1), .d(dd1), .c(cc1));  // open: dp
endmodule

module Hours_Circuit (
);

  wire a0, a1, b0, b1, bcd_converter_1_w0, bcd_converter_1_w1, bcd_converter_1_w2, bcd_converter_1_w3,
       bcd_converter_1_w4, bcd_converter_1_w5, bcd_converter_1_w6, bcd_converter_1_w7, c0, c1, Clk_out, d0,
       d1, e0, e1, f0, f1, g0, g1, n0_24_counter_1_out_4, n0_24_counter_1_out_5, n0_24_counter_1_q0,
       n0_24_counter_1_q1, n0_24_counter_1_q4;

  Clock Clk (.out(Clk_out));
  _0_24_counter u_0_24_counter_1 (
    .q0(n0_24_counter_1_q0), .q1(n0_24_counter_1_q1), .out_4(n0_24_counter_1_out_4),
    .out_5(n0_24_counter_1_out_5), .q4(n0_24_counter_1_q4), .in_1(Clk_out));  // open: out_7
  BCD_converter bcd_converter_1 (
    .i0(1'b0), .i1(n0_24_counter_1_q4), .i2(n0_24_counter_1_out_5), .i3(n0_24_counter_1_out_4),
    .i4(n0_24_counter_1_q1), .i5(n0_24_counter_1_q0), .w0(bcd_converter_1_w0), .w1(bcd_converter_1_w1),
    .w2(bcd_converter_1_w2), .w3(bcd_converter_1_w3), .w4(bcd_converter_1_w4), .w5(bcd_converter_1_w5),
    .w6(bcd_converter_1_w6), .w7(bcd_converter_1_w7));
  Decimal_to_7segment decimal_to_7segment_1 (
    .D(bcd_converter_1_w4), .C(bcd_converter_1_w5), .B(bcd_converter_1_w6), .A(bcd_converter_1_w7), .a_2(a1),
    .b_2(b1), .c_2(c1), .d_2(d1), .e(e1), .f(f1), .g(g1));
  Decimal_to_7segment decimal_to_7segment_2 (
    .D(bcd_converter_1_w0), .C(bcd_converter_1_w1), .B(bcd_converter_1_w2), .A(bcd_converter_1_w3), .a_2(a0),
    .b_2(b0), .c_2(c0), .d_2(d0), .e(e0), .f(f0), .g(g0));
  _7_Segment_Display u_7_segment_display_1 (.g(g0), .f(f0), .a(a0), .b(b0), .e(e0), .d(d0), .c(c0));  // open: dp
  _7_Segment_Display u_7_segment_display_2 (.g(g1), .f(f1), .a(a1), .b(b1), .e(e1), .d(d1), .c(c1));  // open: dp
endmodule

module combinational_for_60sec (
  input  a0,
  input  a1,
  input  a2,
  input  a3,
  input  a4,
  input  a5,
  output x
);

  wire not_1_out, not_2_out;

  not not_1 (not_1_out, a4);
  not not_2 (not_2_out, a5);
  and and_1 (x, a0, a1, a2, a3, not_1_out, not_2_out);
endmodule

module min_sec (
  input  [5:0] in_1,
  input  [5:0] in_2,
  input  in_3,
  input  in_4,
  input  [5:0] in_5,
  input  in_6
);

  wire a0, a1, aa0, aa1, aaa0, aaa1, b0, b1, bb0, bb1, bbb0, bbb1, bcd_converter_1_w0, bcd_converter_1_w1,
       bcd_converter_1_w2, bcd_converter_1_w3, bcd_converter_1_w4, bcd_converter_1_w5, bcd_converter_1_w6,
       bcd_converter_1_w7, bcd_converter_2_w0, bcd_converter_2_w1, bcd_converter_2_w2, bcd_converter_2_w3,
       bcd_converter_2_w4, bcd_converter_2_w5, bcd_converter_2_w6, bcd_converter_2_w7, bcd_converter_3_w0,
       bcd_converter_3_w1, bcd_converter_3_w2, bcd_converter_3_w3, bcd_converter_3_w4, bcd_converter_3_w5,
       bcd_converter_3_w6, bcd_converter_3_w7, c0, c1, cc0, cc1, ccc0, ccc1, clock_1_out, d0, d1, dd0, dd1,
       ddd0, ddd1, e0, e1, ee0, ee1, eee0, eee1, f0, f1, ff0, ff1, fff0, fff1, g0, g1, gg0, gg1, ggg0, ggg1,
       x, y;
  wire [4:0] multiplexer_2_out;
  wire [5:0] multiplexer_1_out, multiplexer_3_out, n0_24_counter_1_q0, n0_59_counter_1_q0, n0_59_counter_2_q0;

  Clock clock_1 (.out(clock_1_out));
  _0_59_Counter u_0_59_counter_1 (
    .q0(n0_59_counter_1_q0[0]), .q1(n0_59_counter_1_q0[1]), .out_5(n0_59_counter_1_q0[2]),
    .out_6(n0_59_counter_1_q0[3]), .q4(n0_59_counter_1_q0[4]), .q5(n0_59_counter_1_q0[5]),
    .in_1(clock_1_out), .out_9(x));  // open: out_4
  Multiplexer #(.width(6)) multiplexer_1 (
    .in0(n0_59_counter_1_q0), .in1(in_2), .out(multiplexer_1_out), .sel(in_4));  // open: en
  BCD_converter bcd_converter_1 (
    .i0(multiplexer_1_out[5]), .i1(multiplexer_1_out[4]), .i2(multiplexer_1_out[3]),
    .i3(multiplexer_1_out[2]), .i4(multiplexer_1_out[1]), .i5(multiplexer_1_out[0]), .w0(bcd_converter_1_w0),
    .w1(bcd_converter_1_w1), .w2(bcd_converter_1_w2), .w3(bcd_converter_1_w3), .w4(bcd_converter_1_w4),
    .w5(bcd_converter_1_w5), .w6(bcd_converter_1_w6), .w7(bcd_converter_1_w7));
  Multiplexer #(.width(6)) multiplexer_2 (
    .in0(n0_24_counter_1_q0), .in1(in_5), .out({n0_24_counter_1_q0[5], multiplexer_2_out}), .sel(in_6));  // open: en
  _0_24_counter u_0_24_counter_1 (
    .q0(n0_24_counter_1_q0[0]), .q1(n0_24_counter_1_q0[1]), .out_4(n0_24_counter_1_q0[2]),
    .out_5(n0_24_counter_1_q0[3]), .q4(n0_24_counter_1_q0[4]), .in_1(y));  // open: out_7
  Decimal_to_7segment decimal_to_7segment_1 (
    .D(bcd_converter_1_w4), .C(bcd_converter_1_w5), .B(bcd_converter_1_w6), .A(bcd_converter_1_w7), .a_2(a1),
    .b_2(b1), .c_2(c1), .d_2(d1), .e(e1), .f(f1), .g(g1));
  Decimal_to_7segment decimal_to_7segment_2 (
    .D(bcd_converter_1_w0), .C(bcd_converter_1_w1), .B(bcd_converter_1_w2), .A(bcd_converter_1_w3), .a_2(a0),
    .b_2(b0), .c_2(c0), .d_2(d0), .e(e0), .f(f0), .g(g0));
  BCD_converter bcd_converter_2 (
    .i0(n0_24_counter_1_q0[5]), .i1(multiplexer_2_out[4]), .i2(multiplexer_2_out[3]),
    .i3(multiplexer_2_out[2]), .i4(multiplexer_2_out[1]), .i5(multiplexer_2_out[0]), .w0(bcd_converter_2_w0),
    .w1(bcd_converter_2_w1), .w2(bcd_converter_2_w2), .w3(bcd_converter_2_w3), .w4(bcd_converter_2_w4),
    .w5(bcd_converter_2_w5), .w6(bcd_converter_2_w6), .w7(bcd_converter_2_w7));
  Decimal_to_7segment decimal_to_7segment_3 (
    .D(bcd_converter_2_w4), .C(bcd_converter_2_w5), .B(bcd_converter_2_w6), .A(bcd_converter_2_w7),
    .a_2(aaa1), .b_2(bbb1), .c_2(ccc1), .d_2(ddd1), .e(eee1), .f(fff1), .g(ggg1));
  Decimal_to_7segment decimal_to_7segment_4 (
    .D(bcd_converter_2_w0), .C(bcd_converter_2_w1), .B(bcd_converter_2_w2), .A(bcd_converter_2_w3),
    .a_2(aaa0), .b_2(bbb0), .c_2(ccc0), .d_2(ddd0), .e(eee0), .f(fff0), .g(ggg0));
  _0_59_Counter u_0_59_counter_2 (
    .q0(n0_59_counter_2_q0[0]), .q1(n0_59_counter_2_q0[1]), .out_5(n0_59_counter_2_q0[2]),
    .out_6(n0_59_counter_2_q0[3]), .q4(n0_59_counter_2_q0[4]), .q5(n0_59_counter_2_q0[5]), .in_1(x), .out_9(y));  // open: out_4
  Multiplexer #(.width(6)) multiplexer_3 (
    .in0(n0_59_counter_2_q0), .in1(in_1), .out(multiplexer_3_out), .sel(in_3));  // open: en
  _7_Segment_Display u_7_segment_display_1 (
    .g(ggg0), .f(fff0), .a(aaa0), .b(bbb0), .e(eee0), .d(ddd0), .c(ccc0));  // open: dp
  _7_Segment_Display u_7_segment_display_2 (
    .g(ggg1), .f(fff1), .a(aaa1), .b(bbb1), .e(eee1), .d(ddd1), .c(ccc1));  // open: dp
  _7_Segment_Display u_7_segment_display_3 (.g(gg0), .f(ff0), .a(aa0), .b(bb0), .e(ee0), .d(dd0), .c(cc0));  // open: dp
  BCD_converter bcd_converter_3 (
    .i0(multiplexer_3_out[5]), .i1(multiplexer_3_out[4]), .i2(multiplexer_3_out[3]),
    .i3(multiplexer_3_out[2]), .i4(multiplexer_3_out[1]), .i5(multiplexer_3_out[0]), .w0(bcd_converter_3_w0),
    .w1(bcd_converter_3_w1), .w2(bcd_converter_3_w2), .w3(bcd_converter_3_w3), .w4(bcd_converter_3_w4),
    .w5(bcd_converter_3_w5), .w6(bcd_converter_3_w6), .w7(bcd_converter_3_w7));
  _7_Segment_Display u_7_segment_display_4 (.g(gg1), .f(ff1), .a(aa1), .b(bb1), .e(ee1), .d(dd1), .c(cc1));  // open: dp
  Decimal_to_7segment decimal_to_7segment_5 (
    .D(bcd_converter_3_w4), .C(bcd_converter_3_w5), .B(bcd_converter_3_w6), .A(bcd_converter_3_w7),
    .a_2(aa1), .b_2(bb1), .c_2(cc1), .d_2(dd1), .e(ee1), .f(ff1), .g(gg1));
  _7_Segment_Display u_7_segment_display_5 (.g(g0), .f(f0), .a(a0), .b(b0), .e(e0), .d(d0), .c(c0));  // open: dp
  Decimal_to_7segment decimal_to_7segment_6 (
    .D(bcd_converter_3_w0), .C(bcd_converter_3_w1), .B(bcd_converter_3_w2), .A(bcd_converter_3_w3),
    .a_2(aa0), .b_2(bb0), .c_2(cc0), .d_2(dd0), .e(ee0), .f(ff0), .g(gg0));
  _7_Segment_Display u_7_segment_display_6 (.g(g1), .f(f1), .a(a1), .b(b1), .e(e1), .d(d1), .c(c1));  // open: dp
  // also tied to GND on the sheet: n0_24_counter_1_q0[5]

  // Notes on the sheet:
  //   TO CHANGE seconds MANUUALLY SET TO 1
  //   To change hours manually set to 1 and enter
  //   To change minutes manually set to 1 and enter
  //   Hour
  //   Minute
  //   second
endmodule

module Minute_Sec_hour (
  output [5:0] out_1,
  output out_2
);

  wire a0, a1, aa0, aa1, aaa0, aaa1, b0, b1, bb0, bb1, bbb0, bbb1, bcd_converter_1_w0, bcd_converter_1_w1,
       bcd_converter_1_w2, bcd_converter_1_w3, bcd_converter_1_w4, bcd_converter_1_w5, bcd_converter_1_w6,
       bcd_converter_1_w7, bcd_converter_2_w0, bcd_converter_2_w1, bcd_converter_2_w2, bcd_converter_2_w3,
       bcd_converter_2_w4, bcd_converter_2_w5, bcd_converter_2_w6, bcd_converter_2_w7, bcd_converter_3_w0,
       bcd_converter_3_w1, bcd_converter_3_w2, bcd_converter_3_w3, bcd_converter_3_w4, bcd_converter_3_w5,
       bcd_converter_3_w6, bcd_converter_3_w7, c0, c1, cc0, cc1, ccc0, ccc1, clock_1_out, d0, d1, dd0, dd1,
       ddd0, ddd1, e0, e1, ee0, ee1, eee0, eee1, f0, f1, ff0, ff1, fff0, fff1, g0, g1, gg0, gg1, ggg0, ggg1,
       n0_24_counter_1_out_4, n0_24_counter_1_out_5, n0_24_counter_1_q0, n0_24_counter_1_q1,
       n0_24_counter_1_q4, n0_59_counter_2_out_5, n0_59_counter_2_out_6, n0_59_counter_2_q0,
       n0_59_counter_2_q1, n0_59_counter_2_q4, n0_59_counter_2_q5, x;

  Clock clock_1 (.out(clock_1_out));
  _0_59_Counter u_0_59_counter_1 (
    .q0(out_1[0]), .q1(out_1[1]), .out_5(out_1[2]), .out_6(out_1[3]), .q4(out_1[4]), .q5(out_1[5]),
    .in_1(clock_1_out), .out_9(x));  // open: out_4
  BCD_converter bcd_converter_1 (
    .i0(out_1[5]), .i1(out_1[4]), .i2(out_1[3]), .i3(out_1[2]), .i4(out_1[1]), .i5(out_1[0]),
    .w0(bcd_converter_1_w0), .w1(bcd_converter_1_w1), .w2(bcd_converter_1_w2), .w3(bcd_converter_1_w3),
    .w4(bcd_converter_1_w4), .w5(bcd_converter_1_w5), .w6(bcd_converter_1_w6), .w7(bcd_converter_1_w7));
  Decimal_to_7segment decimal_to_7segment_1 (
    .D(bcd_converter_1_w4), .C(bcd_converter_1_w5), .B(bcd_converter_1_w6), .A(bcd_converter_1_w7), .a_2(a1),
    .b_2(b1), .c_2(c1), .d_2(d1), .e(e1), .f(f1), .g(g1));
  _0_24_counter u_0_24_counter_1 (
    .q0(n0_24_counter_1_q0), .q1(n0_24_counter_1_q1), .out_4(n0_24_counter_1_out_4),
    .out_5(n0_24_counter_1_out_5), .q4(n0_24_counter_1_q4), .in_1(out_2));  // open: out_7
  Decimal_to_7segment decimal_to_7segment_2 (
    .D(bcd_converter_1_w0), .C(bcd_converter_1_w1), .B(bcd_converter_1_w2), .A(bcd_converter_1_w3), .a_2(a0),
    .b_2(b0), .c_2(c0), .d_2(d0), .e(e0), .f(f0), .g(g0));
  _7_Segment_Display u_7_segment_display_1 (.g(g0), .f(f0), .a(a0), .b(b0), .e(e0), .d(d0), .c(c0));  // open: dp
  BCD_converter bcd_converter_2 (
    .i0(1'b0), .i1(n0_24_counter_1_q4), .i2(n0_24_counter_1_out_5), .i3(n0_24_counter_1_out_4),
    .i4(n0_24_counter_1_q1), .i5(n0_24_counter_1_q0), .w0(bcd_converter_2_w0), .w1(bcd_converter_2_w1),
    .w2(bcd_converter_2_w2), .w3(bcd_converter_2_w3), .w4(bcd_converter_2_w4), .w5(bcd_converter_2_w5),
    .w6(bcd_converter_2_w6), .w7(bcd_converter_2_w7));
  _0_59_Counter u_0_59_counter_2 (
    .q0(n0_59_counter_2_q0), .q1(n0_59_counter_2_q1), .out_5(n0_59_counter_2_out_5),
    .out_6(n0_59_counter_2_out_6), .q4(n0_59_counter_2_q4), .q5(n0_59_counter_2_q5), .in_1(x), .out_9(out_2));  // open: out_4
  _7_Segment_Display u_7_segment_display_2 (.g(g1), .f(f1), .a(a1), .b(b1), .e(e1), .d(d1), .c(c1));  // open: dp
  Decimal_to_7segment decimal_to_7segment_3 (
    .D(bcd_converter_2_w4), .C(bcd_converter_2_w5), .B(bcd_converter_2_w6), .A(bcd_converter_2_w7),
    .a_2(aaa1), .b_2(bbb1), .c_2(ccc1), .d_2(ddd1), .e(eee1), .f(fff1), .g(ggg1));
  Decimal_to_7segment decimal_to_7segment_4 (
    .D(bcd_converter_2_w0), .C(bcd_converter_2_w1), .B(bcd_converter_2_w2), .A(bcd_converter_2_w3),
    .a_2(aaa0), .b_2(bbb0), .c_2(ccc0), .d_2(ddd0), .e(eee0), .f(fff0), .g(ggg0));
  BCD_converter bcd_converter_3 (
    .i0(n0_59_counter_2_q5), .i1(n0_59_counter_2_q4), .i2(n0_59_counter_2_out_6), .i3(n0_59_counter_2_out_5),
    .i4(n0_59_counter_2_q1), .i5(n0_59_counter_2_q0), .w0(bcd_converter_3_w0), .w1(bcd_converter_3_w1),
    .w2(bcd_converter_3_w2), .w3(bcd_converter_3_w3), .w4(bcd_converter_3_w4), .w5(bcd_converter_3_w5),
    .w6(bcd_converter_3_w6), .w7(bcd_converter_3_w7));
  _7_Segment_Display u_7_segment_display_3 (
    .g(ggg0), .f(fff0), .a(aaa0), .b(bbb0), .e(eee0), .d(ddd0), .c(ccc0));  // open: dp
  _7_Segment_Display u_7_segment_display_4 (
    .g(ggg1), .f(fff1), .a(aaa1), .b(bbb1), .e(eee1), .d(ddd1), .c(ccc1));  // open: dp
  Decimal_to_7segment decimal_to_7segment_5 (
    .D(bcd_converter_3_w4), .C(bcd_converter_3_w5), .B(bcd_converter_3_w6), .A(bcd_converter_3_w7),
    .a_2(aa1), .b_2(bb1), .c_2(cc1), .d_2(dd1), .e(ee1), .f(ff1), .g(gg1));
  Decimal_to_7segment decimal_to_7segment_6 (
    .D(bcd_converter_3_w0), .C(bcd_converter_3_w1), .B(bcd_converter_3_w2), .A(bcd_converter_3_w3),
    .a_2(aa0), .b_2(bb0), .c_2(cc0), .d_2(dd0), .e(ee0), .f(ff0), .g(gg0));
  _7_Segment_Display u_7_segment_display_5 (.g(gg0), .f(ff0), .a(aa0), .b(bb0), .e(ee0), .d(dd0), .c(cc0));  // open: dp
  _7_Segment_Display u_7_segment_display_6 (.g(gg1), .f(ff1), .a(aa1), .b(bb1), .e(ee1), .d(dd1), .c(cc1));  // open: dp

  // Other names for the same wires on the sheet: y = out_2

  // Notes on the sheet:
  //   Second
  //   hours
  //   Minute
endmodule

module sec_min_hour_manual (
  input  [5:0] in_1,
  input  [5:0] in_2,
  input  in_3,
  input  in_4,
  input  [5:0] in_5,
  input  in_6
);

  wire a0, a1, aa0, aa1, aaa0, aaa1, b0, b1, bb0, bb1, bbb0, bbb1, bcd_converter_1_w0, bcd_converter_1_w1,
       bcd_converter_1_w2, bcd_converter_1_w3, bcd_converter_1_w4, bcd_converter_1_w5, bcd_converter_1_w6,
       bcd_converter_1_w7, bcd_converter_2_w0, bcd_converter_2_w1, bcd_converter_2_w2, bcd_converter_2_w3,
       bcd_converter_2_w4, bcd_converter_2_w5, bcd_converter_2_w6, bcd_converter_2_w7, bcd_converter_3_w0,
       bcd_converter_3_w1, bcd_converter_3_w2, bcd_converter_3_w3, bcd_converter_3_w4, bcd_converter_3_w5,
       bcd_converter_3_w6, bcd_converter_3_w7, c0, c1, cc0, cc1, ccc0, ccc1, clock_1_out, d0, d1, dd0, dd1,
       ddd0, ddd1, e0, e1, ee0, ee1, eee0, eee1, f0, f1, ff0, ff1, fff0, fff1, g0, g1, gg0, gg1, ggg0, ggg1,
       x, y;
  wire [4:0] multiplexer_2_out;
  wire [5:0] multiplexer_1_out, multiplexer_3_out, n0_24_counter_1_q0, n0_59_counter_1_q0, n0_59_counter_2_q0;

  Clock clock_1 (.out(clock_1_out));
  _7_Segment_Display u_7_segment_display_1 (
    .g(ggg0), .f(fff0), .a(aaa0), .b(bbb0), .e(eee0), .d(ddd0), .c(ccc0));  // open: dp
  _0_59_Counter u_0_59_counter_1 (
    .q0(n0_59_counter_1_q0[0]), .q1(n0_59_counter_1_q0[1]), .out_5(n0_59_counter_1_q0[2]),
    .out_6(n0_59_counter_1_q0[3]), .q4(n0_59_counter_1_q0[4]), .q5(n0_59_counter_1_q0[5]),
    .in_1(clock_1_out), .out_9(x));  // open: out_4
  Multiplexer #(.width(6)) multiplexer_1 (
    .in0(n0_59_counter_1_q0), .in1(in_2), .out(multiplexer_1_out), .sel(in_4));  // open: en
  _7_Segment_Display u_7_segment_display_2 (
    .g(ggg1), .f(fff1), .a(aaa1), .b(bbb1), .e(eee1), .d(ddd1), .c(ccc1));  // open: dp
  BCD_converter bcd_converter_1 (
    .i0(multiplexer_1_out[5]), .i1(multiplexer_1_out[4]), .i2(multiplexer_1_out[3]),
    .i3(multiplexer_1_out[2]), .i4(multiplexer_1_out[1]), .i5(multiplexer_1_out[0]), .w0(bcd_converter_1_w0),
    .w1(bcd_converter_1_w1), .w2(bcd_converter_1_w2), .w3(bcd_converter_1_w3), .w4(bcd_converter_1_w4),
    .w5(bcd_converter_1_w5), .w6(bcd_converter_1_w6), .w7(bcd_converter_1_w7));
  Multiplexer #(.width(6)) multiplexer_2 (
    .in0(n0_24_counter_1_q0), .in1(in_5), .out({n0_24_counter_1_q0[5], multiplexer_2_out}), .sel(in_6));  // open: en
  _0_24_counter u_0_24_counter_1 (
    .q0(n0_24_counter_1_q0[0]), .q1(n0_24_counter_1_q0[1]), .out_4(n0_24_counter_1_q0[2]),
    .out_5(n0_24_counter_1_q0[3]), .q4(n0_24_counter_1_q0[4]), .in_1(y));  // open: out_7
  _7_Segment_Display u_7_segment_display_3 (.g(gg0), .f(ff0), .a(aa0), .b(bb0), .e(ee0), .d(dd0), .c(cc0));  // open: dp
  Decimal_to_7segment decimal_to_7segment_1 (
    .D(bcd_converter_1_w4), .C(bcd_converter_1_w5), .B(bcd_converter_1_w6), .A(bcd_converter_1_w7), .a_2(a1),
    .b_2(b1), .c_2(c1), .d_2(d1), .e(e1), .f(f1), .g(g1));
  Decimal_to_7segment decimal_to_7segment_2 (
    .D(bcd_converter_1_w0), .C(bcd_converter_1_w1), .B(bcd_converter_1_w2), .A(bcd_converter_1_w3), .a_2(a0),
    .b_2(b0), .c_2(c0), .d_2(d0), .e(e0), .f(f0), .g(g0));
  _7_Segment_Display u_7_segment_display_4 (.g(gg1), .f(ff1), .a(aa1), .b(bb1), .e(ee1), .d(dd1), .c(cc1));  // open: dp
  BCD_converter bcd_converter_2 (
    .i0(n0_24_counter_1_q0[5]), .i1(multiplexer_2_out[4]), .i2(multiplexer_2_out[3]),
    .i3(multiplexer_2_out[2]), .i4(multiplexer_2_out[1]), .i5(multiplexer_2_out[0]), .w0(bcd_converter_2_w0),
    .w1(bcd_converter_2_w1), .w2(bcd_converter_2_w2), .w3(bcd_converter_2_w3), .w4(bcd_converter_2_w4),
    .w5(bcd_converter_2_w5), .w6(bcd_converter_2_w6), .w7(bcd_converter_2_w7));
  _7_Segment_Display u_7_segment_display_5 (.g(g0), .f(f0), .a(a0), .b(b0), .e(e0), .d(d0), .c(c0));  // open: dp
  Decimal_to_7segment decimal_to_7segment_3 (
    .D(bcd_converter_2_w4), .C(bcd_converter_2_w5), .B(bcd_converter_2_w6), .A(bcd_converter_2_w7),
    .a_2(aaa1), .b_2(bbb1), .c_2(ccc1), .d_2(ddd1), .e(eee1), .f(fff1), .g(ggg1));
  Decimal_to_7segment decimal_to_7segment_4 (
    .D(bcd_converter_2_w0), .C(bcd_converter_2_w1), .B(bcd_converter_2_w2), .A(bcd_converter_2_w3),
    .a_2(aaa0), .b_2(bbb0), .c_2(ccc0), .d_2(ddd0), .e(eee0), .f(fff0), .g(ggg0));
  _7_Segment_Display u_7_segment_display_6 (.g(g1), .f(f1), .a(a1), .b(b1), .e(e1), .d(d1), .c(c1));  // open: dp
  _0_59_Counter u_0_59_counter_2 (
    .q0(n0_59_counter_2_q0[0]), .q1(n0_59_counter_2_q0[1]), .out_5(n0_59_counter_2_q0[2]),
    .out_6(n0_59_counter_2_q0[3]), .q4(n0_59_counter_2_q0[4]), .q5(n0_59_counter_2_q0[5]), .in_1(x), .out_9(y));  // open: out_4
  Multiplexer #(.width(6)) multiplexer_3 (
    .in0(n0_59_counter_2_q0), .in1(in_1), .out(multiplexer_3_out), .sel(in_3));  // open: en
  BCD_converter bcd_converter_3 (
    .i0(multiplexer_3_out[5]), .i1(multiplexer_3_out[4]), .i2(multiplexer_3_out[3]),
    .i3(multiplexer_3_out[2]), .i4(multiplexer_3_out[1]), .i5(multiplexer_3_out[0]), .w0(bcd_converter_3_w0),
    .w1(bcd_converter_3_w1), .w2(bcd_converter_3_w2), .w3(bcd_converter_3_w3), .w4(bcd_converter_3_w4),
    .w5(bcd_converter_3_w5), .w6(bcd_converter_3_w6), .w7(bcd_converter_3_w7));
  Decimal_to_7segment decimal_to_7segment_5 (
    .D(bcd_converter_3_w4), .C(bcd_converter_3_w5), .B(bcd_converter_3_w6), .A(bcd_converter_3_w7),
    .a_2(aa1), .b_2(bb1), .c_2(cc1), .d_2(dd1), .e(ee1), .f(ff1), .g(gg1));
  Decimal_to_7segment decimal_to_7segment_6 (
    .D(bcd_converter_3_w0), .C(bcd_converter_3_w1), .B(bcd_converter_3_w2), .A(bcd_converter_3_w3),
    .a_2(aa0), .b_2(bb0), .c_2(cc0), .d_2(dd0), .e(ee0), .f(ff0), .g(gg0));
  // also tied to GND on the sheet: n0_24_counter_1_q0[5]

  // Notes on the sheet:
  //   To change secondamanully set to 1 and enter
  //   Hour
  //   To change hours manually set to 1 and enter
  //   Minute
  //   To change minutes manually set to 1 and enter
  //   second
endmodule

module Alarm_and_set_alarm (
  input  [5:0] in_1,
  input  [5:0] in_2,
  input  [5:0] in_3
);

  wire bcd_converter_1_w0, bcd_converter_1_w1, bcd_converter_1_w2, bcd_converter_1_w3, bcd_converter_1_w4,
       bcd_converter_1_w5, bcd_converter_1_w6, bcd_converter_1_w7, bcd_converter_2_w0, bcd_converter_2_w1,
       bcd_converter_2_w2, bcd_converter_2_w3, bcd_converter_2_w4, bcd_converter_2_w5, bcd_converter_2_w6,
       bcd_converter_2_w7, bcd_converter_3_w0, bcd_converter_3_w1, bcd_converter_3_w2, bcd_converter_3_w3,
       bcd_converter_3_w4, bcd_converter_3_w5, bcd_converter_3_w6, bcd_converter_3_w7, h0, h1, hh0, hh1,
       hhh0, hhh1, i0, i1, ii0, ii1, iii0, iii1, j0, j1, jj0, jj1, jjj0, jjj1, k0, k1, kk0, kk1, kkk0, kkk1,
       l0, l1, ll0, ll1, lll0, lll1, m0, m1, mm0, mm1, mmm0, mmm1, n0, n1, nn0, nn1, nnn0, nnn1;

  BCD_converter bcd_converter_1 (
    .i0(in_2[5]), .i1(in_2[4]), .i2(in_2[3]), .i3(in_2[2]), .i4(in_2[1]), .i5(in_2[0]),
    .w0(bcd_converter_1_w0), .w1(bcd_converter_1_w1), .w2(bcd_converter_1_w2), .w3(bcd_converter_1_w3),
    .w4(bcd_converter_1_w4), .w5(bcd_converter_1_w5), .w6(bcd_converter_1_w6), .w7(bcd_converter_1_w7));
  Decimal_to_7segment decimal_to_7segment_1 (
    .D(bcd_converter_1_w4), .C(bcd_converter_1_w5), .B(bcd_converter_1_w6), .A(bcd_converter_1_w7), .a_2(h1),
    .b_2(i1), .c_2(j1), .d_2(k1), .e(l1), .f(m1), .g(n1));
  Decimal_to_7segment decimal_to_7segment_2 (
    .D(bcd_converter_1_w0), .C(bcd_converter_1_w1), .B(bcd_converter_1_w2), .A(bcd_converter_1_w3), .a_2(h0),
    .b_2(i0), .c_2(j0), .d_2(k0), .e(l0), .f(m0), .g(n0));
  BCD_converter bcd_converter_2 (
    .i0(in_3[5]), .i1(in_3[4]), .i2(in_3[3]), .i3(in_3[2]), .i4(in_3[1]), .i5(in_3[0]),
    .w0(bcd_converter_2_w0), .w1(bcd_converter_2_w1), .w2(bcd_converter_2_w2), .w3(bcd_converter_2_w3),
    .w4(bcd_converter_2_w4), .w5(bcd_converter_2_w5), .w6(bcd_converter_2_w6), .w7(bcd_converter_2_w7));
  Decimal_to_7segment decimal_to_7segment_3 (
    .D(bcd_converter_2_w4), .C(bcd_converter_2_w5), .B(bcd_converter_2_w6), .A(bcd_converter_2_w7),
    .a_2(hhh1), .b_2(iii1), .c_2(jjj1), .d_2(kkk1), .e(lll1), .f(mmm1), .g(nnn1));
  Decimal_to_7segment decimal_to_7segment_4 (
    .D(bcd_converter_2_w0), .C(bcd_converter_2_w1), .B(bcd_converter_2_w2), .A(bcd_converter_2_w3),
    .a_2(hhh0), .b_2(iii0), .c_2(jjj0), .d_2(kkk0), .e(lll0), .f(mmm0), .g(nnn0));
  _7_Segment_Display u_7_segment_display_1 (
    .g(nnn0), .f(mmm0), .a(hhh0), .b(iii0), .e(lll0), .d(kkk0), .c(jjj0));  // open: dp
  _7_Segment_Display u_7_segment_display_2 (
    .g(nnn1), .f(mmm1), .a(hhh1), .b(iii1), .e(lll1), .d(kkk1), .c(jjj1));  // open: dp
  _7_Segment_Display u_7_segment_display_3 (.g(nn0), .f(mm0), .a(hh0), .b(ii0), .e(ll0), .d(kk0), .c(jj0));  // open: dp
  BCD_converter bcd_converter_3 (
    .i0(in_1[5]), .i1(in_1[4]), .i2(in_1[3]), .i3(in_1[2]), .i4(in_1[1]), .i5(in_1[0]),
    .w0(bcd_converter_3_w0), .w1(bcd_converter_3_w1), .w2(bcd_converter_3_w2), .w3(bcd_converter_3_w3),
    .w4(bcd_converter_3_w4), .w5(bcd_converter_3_w5), .w6(bcd_converter_3_w6), .w7(bcd_converter_3_w7));
  _7_Segment_Display u_7_segment_display_4 (.g(nn1), .f(mm1), .a(hh1), .b(ii1), .e(ll1), .d(kk1), .c(jj1));  // open: dp
  Decimal_to_7segment decimal_to_7segment_5 (
    .D(bcd_converter_3_w4), .C(bcd_converter_3_w5), .B(bcd_converter_3_w6), .A(bcd_converter_3_w7),
    .a_2(hh1), .b_2(ii1), .c_2(jj1), .d_2(kk1), .e(ll1), .f(mm1), .g(nn1));
  _7_Segment_Display u_7_segment_display_5 (.g(n0), .f(m0), .a(h0), .b(i0), .e(l0), .d(k0), .c(j0));  // open: dp
  Decimal_to_7segment decimal_to_7segment_6 (
    .D(bcd_converter_3_w0), .C(bcd_converter_3_w1), .B(bcd_converter_3_w2), .A(bcd_converter_3_w3),
    .a_2(hh0), .b_2(ii0), .c_2(jj0), .d_2(kk0), .e(ll0), .f(mm0), .g(nn0));
  _7_Segment_Display u_7_segment_display_6 (.g(n1), .f(m1), .a(h1), .b(i1), .e(l1), .d(k1), .c(j1));  // open: dp
  // also tied to GND on the sheet: in_3[5]

  // Notes on the sheet:
  //   Set seconds part of the alarm
  //   To change hours manually set to 1 and enter
  //   set minutes part of alarm 
  //   Hour
  //   Minute
  //   second
endmodule

module led_test (
  input  [5:0] in_1,
  input  [5:0] in_2,
  input  in_3,
  input  in_4,
  input  [5:0] in_5,
  input  [5:0] in_6,
  input  [5:0] in_7,
  input  in_8,
  input  [5:0] in_9,
  output [3:0] out_10,
  output [3:0] out_11,
  output [3:0] out_12,
  output [3:0] out_13,
  output [3:0] out_14,
  output [3:0] out_15,
  output [3:0] out_16,
  output [3:0] out_17,
  output [3:0] out_18,
  output [3:0] out_19,
  output [3:0] out_20,
  output [3:0] out_21
);

  wire a0, a1, aa0, aa1, aaa0, aaa1, and_1_out, b0, b1, bb0, bb1, bbb0, bbb1, bcd_converter_1_w1,
       bcd_converter_3_w2, bcd_converter_3_w6, c0, c1, cc0, cc1, ccc0, ccc1, clock_1_out, comparator_1_eq,
       comparator_2_eq, comparator_3_eq, comparator_4_eq, comparator_5_eq, comparator_6_eq, d0, d1, dd0, dd1,
       ddd0, ddd1, e0, e1, ee0, ee1, eee0, eee1, f0, f1, ff0, ff1, fff0, fff1, g0, g1, gg0, gg1, ggg0, ggg1,
       h0, h1, hh0, hh1, hhh0, hhh1, i0, i1, ii0, ii1, iii0, iii1, j0, j1, jj0, jj1, jjj0, jjj1, k0, k1, kk0,
       kk1, kkk0, kkk1, l0, l1, ll0, ll1, lll0, lll1, m0, m1, mm0, mm1, mmm0, mmm1, n0, n1, nn0, nn1, nnn0,
       nnn1, x, y;
  wire [4:0] multiplexer_2_out;
  wire [5:0] multiplexer_1_out, multiplexer_3_out, n0_24_counter_1_q0, n0_59_counter_1_q0, n0_59_counter_2_q0;

  Clock clock_1 (.out(clock_1_out));
  _7_Segment_Display u_7_segment_display_1 (
    .g(ggg0), .f(fff0), .a(aaa0), .b(bbb0), .e(eee0), .d(ddd0), .c(ccc0));  // open: dp
  _0_59_Counter u_0_59_counter_1 (
    .q0(n0_59_counter_1_q0[0]), .q1(n0_59_counter_1_q0[1]), .out_5(n0_59_counter_1_q0[2]),
    .out_6(n0_59_counter_1_q0[3]), .q4(n0_59_counter_1_q0[4]), .q5(n0_59_counter_1_q0[5]),
    .in_1(clock_1_out), .out_9(x));  // open: out_4
  Multiplexer #(.width(6)) multiplexer_1 (
    .in0(n0_59_counter_1_q0), .in1(in_2), .out(multiplexer_1_out), .sel(in_4));  // open: en
  _7_Segment_Display u_7_segment_display_2 (
    .g(ggg1), .f(fff1), .a(aaa1), .b(bbb1), .e(eee1), .d(ddd1), .c(ccc1));  // open: dp
  BCD_converter bcd_converter_1 (
    .i0(multiplexer_1_out[5]), .i1(multiplexer_1_out[4]), .i2(multiplexer_1_out[3]),
    .i3(multiplexer_1_out[2]), .i4(multiplexer_1_out[1]), .i5(multiplexer_1_out[0]), .w0(out_14[3]),
    .w1(bcd_converter_1_w1), .w2(out_14[2]), .w3(out_14[1]), .w4(out_13[3]), .w5(out_13[2]), .w6(out_13[1]),
    .w7(out_13[0]));
  Multiplexer #(.width(6)) multiplexer_2 (
    .in0(n0_24_counter_1_q0), .in1(in_6), .out({n0_24_counter_1_q0[5], multiplexer_2_out}), .sel(in_8));  // open: en
  _0_24_counter u_0_24_counter_1 (
    .q0(n0_24_counter_1_q0[0]), .q1(n0_24_counter_1_q0[1]), .out_4(n0_24_counter_1_q0[2]),
    .out_5(n0_24_counter_1_q0[3]), .q4(n0_24_counter_1_q0[4]), .in_1(y));  // open: out_7
  _7_Segment_Display u_7_segment_display_3 (.g(gg0), .f(ff0), .a(aa0), .b(bb0), .e(ee0), .d(dd0), .c(cc0));  // open: dp
  Decimal_to_7segment decimal_to_7segment_1 (
    .D(out_13[3]), .C(out_13[2]), .B(out_13[1]), .A(out_13[0]), .a_2(a1), .b_2(b1), .c_2(c1), .d_2(d1),
    .e(e1), .f(f1), .g(g1));
  Decimal_to_7segment decimal_to_7segment_2 (
    .D(out_14[3]), .C(bcd_converter_1_w1), .B(out_14[2]), .A(out_14[1]), .a_2(a0), .b_2(b0), .c_2(c0),
    .d_2(d0), .e(e0), .f(f0), .g(g0));
  _7_Segment_Display u_7_segment_display_4 (.g(gg1), .f(ff1), .a(aa1), .b(bb1), .e(ee1), .d(dd1), .c(cc1));  // open: dp
  BCD_converter bcd_converter_2 (
    .i0(n0_24_counter_1_q0[5]), .i1(multiplexer_2_out[4]), .i2(multiplexer_2_out[3]),
    .i3(multiplexer_2_out[2]), .i4(multiplexer_2_out[1]), .i5(multiplexer_2_out[0]), .w0(out_16[3]),
    .w1(out_16[2]), .w2(out_16[1]), .w3(out_16[0]), .w4(out_19[3]), .w5(out_19[2]), .w6(out_19[1]),
    .w7(out_19[0]));
  _7_Segment_Display u_7_segment_display_5 (.g(g0), .f(f0), .a(a0), .b(b0), .e(e0), .d(d0), .c(c0));  // open: dp
  Decimal_to_7segment decimal_to_7segment_3 (
    .D(out_19[3]), .C(out_19[2]), .B(out_19[1]), .A(out_19[0]), .a_2(aaa1), .b_2(bbb1), .c_2(ccc1),
    .d_2(ddd1), .e(eee1), .f(fff1), .g(ggg1));
  Decimal_to_7segment decimal_to_7segment_4 (
    .D(out_16[3]), .C(out_16[2]), .B(out_16[1]), .A(out_16[0]), .a_2(aaa0), .b_2(bbb0), .c_2(ccc0),
    .d_2(ddd0), .e(eee0), .f(fff0), .g(ggg0));
  _7_Segment_Display u_7_segment_display_6 (.g(g1), .f(f1), .a(a1), .b(b1), .e(e1), .d(d1), .c(c1));  // open: dp
  _0_59_Counter u_0_59_counter_2 (
    .q0(n0_59_counter_2_q0[0]), .q1(n0_59_counter_2_q0[1]), .out_5(n0_59_counter_2_q0[2]),
    .out_6(n0_59_counter_2_q0[3]), .q4(n0_59_counter_2_q0[4]), .q5(n0_59_counter_2_q0[5]), .in_1(x), .out_9(y));  // open: out_4
  Multiplexer #(.width(6)) multiplexer_3 (
    .in0(n0_59_counter_2_q0), .in1(in_1), .out(multiplexer_3_out), .sel(in_3));  // open: en
  BCD_converter bcd_converter_3 (
    .i0(multiplexer_3_out[5]), .i1(multiplexer_3_out[4]), .i2(multiplexer_3_out[3]),
    .i3(multiplexer_3_out[2]), .i4(multiplexer_3_out[1]), .i5(multiplexer_3_out[0]), .w0(out_10[3]),
    .w1(out_10[2]), .w2(bcd_converter_3_w2), .w3(out_10[1]), .w4(out_11[3]), .w5(out_11[2]),
    .w6(bcd_converter_3_w6), .w7(out_11[1]));
  Comparator #(.width(4)) comparator_1 (.a(out_21), .b(out_19), .eq(comparator_1_eq));  // open: gt, lt
  Comparator #(.width(4)) comparator_2 (.a(out_18), .b(out_13), .eq(comparator_2_eq));  // open: gt, lt
  Comparator #(.width(4)) comparator_3 (
    .a(out_15), .b({out_14[3:1], out_14[3]}), .eq(comparator_3_eq));  // open: gt, lt
  Comparator #(.width(4)) comparator_4 (.a(out_16), .b(out_20), .eq(comparator_4_eq));  // open: gt, lt
  Decimal_to_7segment decimal_to_7segment_5 (
    .D(out_11[3]), .C(out_11[2]), .B(bcd_converter_3_w6), .A(out_11[1]), .a_2(aa1), .b_2(bb1), .c_2(cc1),
    .d_2(dd1), .e(ee1), .f(ff1), .g(gg1));
  Decimal_to_7segment decimal_to_7segment_6 (
    .D(out_10[3]), .C(out_10[2]), .B(bcd_converter_3_w2), .A(out_10[1]), .a_2(aa0), .b_2(bb0), .c_2(cc0),
    .d_2(dd0), .e(ee0), .f(ff0), .g(gg0));
  BCD_converter bcd_converter_4 (
    .i0(in_7[5]), .i1(in_7[4]), .i2(in_7[3]), .i3(in_7[2]), .i4(in_7[1]), .i5(in_7[0]), .w0(out_15[3]),
    .w1(out_15[2]), .w2(out_15[1]), .w3(out_15[0]), .w4(out_18[3]), .w5(out_18[2]), .w6(out_18[1]),
    .w7(out_18[0]));
  Decimal_to_7segment decimal_to_7segment_7 (
    .D(out_18[3]), .C(out_18[2]), .B(out_18[1]), .A(out_18[0]), .a_2(h1), .b_2(i1), .c_2(j1), .d_2(k1),
    .e(l1), .f(m1), .g(n1));
  Decimal_to_7segment decimal_to_7segment_8 (
    .D(out_15[3]), .C(out_15[2]), .B(out_15[1]), .A(out_15[0]), .a_2(h0), .b_2(i0), .c_2(j0), .d_2(k0),
    .e(l0), .f(m0), .g(n0));
  Comparator #(.width(4)) comparator_5 (
    .a({out_10[3:1], out_10[2]}), .b(out_12), .eq(comparator_5_eq));  // open: gt, lt
  Comparator #(.width(4)) comparator_6 (
    .a({out_11[3:1], out_11[3]}), .b(out_17), .eq(comparator_6_eq));  // open: gt, lt
  BCD_converter bcd_converter_5 (
    .i0(in_9[5]), .i1(in_9[4]), .i2(in_9[3]), .i3(in_9[2]), .i4(in_9[1]), .i5(in_9[0]), .w0(out_20[3]),
    .w1(out_20[2]), .w2(out_20[1]), .w3(out_20[0]), .w4(out_21[3]), .w5(out_21[2]), .w6(out_21[1]),
    .w7(out_21[0]));
  Decimal_to_7segment decimal_to_7segment_9 (
    .D(out_21[3]), .C(out_21[2]), .B(out_21[1]), .A(out_21[0]), .a_2(hhh1), .b_2(iii1), .c_2(jjj1),
    .d_2(kkk1), .e(lll1), .f(mmm1), .g(nnn1));
  and and_1 (and_1_out, comparator_5_eq, comparator_2_eq, comparator_6_eq, comparator_1_eq, comparator_4_eq, comparator_3_eq);
  Decimal_to_7segment decimal_to_7segment_10 (
    .D(out_20[3]), .C(out_20[2]), .B(out_20[1]), .A(out_20[0]), .a_2(hhh0), .b_2(iii0), .c_2(jjj0),
    .d_2(kkk0), .e(lll0), .f(mmm0), .g(nnn0));
  _7_Segment_Display u_7_segment_display_7 (
    .g(nnn0), .f(mmm0), .a(hhh0), .b(iii0), .e(lll0), .d(kkk0), .c(jjj0));  // open: dp
  LED led_1 (.in(and_1_out));
  _7_Segment_Display u_7_segment_display_8 (
    .g(nnn1), .f(mmm1), .a(hhh1), .b(iii1), .e(lll1), .d(kkk1), .c(jjj1));  // open: dp
  _7_Segment_Display u_7_segment_display_9 (.g(nn0), .f(mm0), .a(hh0), .b(ii0), .e(ll0), .d(kk0), .c(jj0));  // open: dp
  BCD_converter bcd_converter_6 (
    .i0(in_5[5]), .i1(in_5[4]), .i2(in_5[3]), .i3(in_5[2]), .i4(in_5[1]), .i5(in_5[0]), .w0(out_12[3]),
    .w1(out_12[2]), .w2(out_12[1]), .w3(out_12[0]), .w4(out_17[3]), .w5(out_17[2]), .w6(out_17[1]),
    .w7(out_17[0]));
  _7_Segment_Display u_7_segment_display_10 (
    .g(nn1), .f(mm1), .a(hh1), .b(ii1), .e(ll1), .d(kk1), .c(jj1));  // open: dp
  Decimal_to_7segment decimal_to_7segment_11 (
    .D(out_17[3]), .C(out_17[2]), .B(out_17[1]), .A(out_17[0]), .a_2(hh1), .b_2(ii1), .c_2(jj1), .d_2(kk1),
    .e(ll1), .f(mm1), .g(nn1));
  Decimal_to_7segment decimal_to_7segment_12 (
    .D(out_12[3]), .C(out_12[2]), .B(out_12[1]), .A(out_12[0]), .a_2(hh0), .b_2(ii0), .c_2(jj0), .d_2(kk0),
    .e(ll0), .f(mm0), .g(nn0));
  _7_Segment_Display u_7_segment_display_11 (.g(n0), .f(m0), .a(h0), .b(i0), .e(l0), .d(k0), .c(j0));  // open: dp
  _7_Segment_Display u_7_segment_display_12 (.g(n1), .f(m1), .a(h1), .b(i1), .e(l1), .d(k1), .c(j1));  // open: dp

  assign out_10[0] = out_10[2];
  assign out_11[0] = out_11[3];
  assign out_14[0] = out_14[3];
  // also tied to GND on the sheet: {n0_24_counter_1_q0[5], in_9[5]}

  // Notes on the sheet:
  //   To change secondamanully set to 1 and enter
  //   Hour
  //   To change hours manually set to 1 and enter
  //   Minute
  //   To change minutes manually set to 1 and enter
  //   second
  //   Set seconds part of the alarm
  //   set hour part of alarm
  //   set minutes part of alarm 
  //   Hour
  //   ALARM LIGHT
  //   Minute
  //   second
endmodule

module _0_60_counter (
  input  in_1,
  output q0,
  output q1,
  output [5:0] out_4,
  output out_5,
  output out_6,
  output q4,
  output q5,
  output out_9
);

  wire d_ff_1_qn, d_ff_2_qn, d_ff_3_qn, d_ff_4_qn, d_ff_5_qn, d_ff_6_qn;

  D_Flip_Flop d_ff_1 (.clk(in_1), .D(d_ff_1_qn), .Q(out_4[0]), .Qn(d_ff_1_qn), .reset(out_9));  // open: preset, en
  D_Flip_Flop d_ff_2 (.clk(d_ff_1_qn), .D(d_ff_2_qn), .Q(out_4[1]), .Qn(d_ff_2_qn), .reset(out_9));  // open: preset, en
  D_Flip_Flop d_ff_3 (.clk(d_ff_2_qn), .D(d_ff_3_qn), .Q(out_4[2]), .Qn(d_ff_3_qn), .reset(out_9));  // open: preset, en
  D_Flip_Flop d_ff_4 (.clk(d_ff_3_qn), .D(d_ff_4_qn), .Q(out_4[3]), .Qn(d_ff_4_qn), .reset(out_9));  // open: preset, en
  D_Flip_Flop d_ff_5 (.clk(d_ff_4_qn), .D(d_ff_5_qn), .Q(out_4[4]), .Qn(d_ff_5_qn), .reset(out_9));  // open: preset, en
  D_Flip_Flop d_ff_6 (.clk(d_ff_5_qn), .D(d_ff_6_qn), .Q(out_4[5]), .Qn(d_ff_6_qn), .reset(out_9));  // open: preset, en
  and and_1 (out_9, out_4[5], out_4[4], out_4[3], out_4[2], out_4[0]);

  assign out_5 = out_4[2];
  assign out_6 = out_4[3];
  assign q0 = out_4[0];
  assign q1 = out_4[1];
  assign q4 = out_4[4];
  assign q5 = out_4[5];

  // Notes on the sheet:
  //   q2
  //   q3
endmodule
